// Logisim project bruce.circ as structural Verilog: 1 circuit, main circuit main
module main (
  input  WRn,
  input  RDn,
  input  TB10,
  input  TB11,
  input  ACPUn,
  output CS1n,
  output CS2n,
  output CS3n,
  output CS4n,
  output DIR,
  output DB1En,
  output DB2En,
  output XWRn
);

  ROM #(.addrWidth(5)) rom_1 (
    .addr({ACPUn, TB11, TB10, RDn, WRn}), .data({XWRn, DB2En, DB1En, DIR, CS4n, CS3n, CS2n, CS1n}));

  // Notes on the sheet:
  //   contents of rom_1 (hex, n*v repeats v):
  //   ff ce 5e 7e ff cd 5d 7d ff 8b fb fb ff 87 17 77 4*fa 4*f9 4*f6 4*f5
endmodule
